// Logisim project Cpu8Bits.circ as structural Verilog: 9 circuits, main circuit main
module main (
  input  in_1
);

  wire alu_1_neg_flag, alu_1_pos_flag, alu_1_zero_flag, and_1_out, and_2_out, and_3_out, clock_1_out,
       control_unit_1_vers_alu, flag_reg_1_neg_flag, flag_reg_1_pos_flag, flag_reg_1_zero_flag, not_1_out,
       not_2_out;
  wire [6:0] bin_to_dec_1_n1, demultiplexer_1_out1, demultiplexer_1_out2, demultiplexer_1_out3;
  wire [7:0] ab_sub_reg_1_a_out, ab_sub_reg_1_b_out, control_unit_1_value, R1_reg_out;
  wire [14:0] control_unit_1_cu_instruction;

  Demultiplexer #(.select(2), .width(7)) demultiplexer_1 (
    .out1(demultiplexer_1_out1), .out2(demultiplexer_1_out2), .out3(demultiplexer_1_out3),
    .in(bin_to_dec_1_n1), .sel(control_unit_1_cu_instruction[12:11]));  // open: out0
  Clock clock_1 (.out(clock_1_out));
  LED led_1 (.in(R1_reg_out[0]));
  LED led_2 (.in(R1_reg_out[1]));
  LED led_3 (.in(R1_reg_out[2]));
  LED led_4 (.in(R1_reg_out[3]));
  LED led_5 (.in(R1_reg_out[4]));
  LED led_6 (.in(R1_reg_out[5]));
  LED led_7 (.in(R1_reg_out[6]));
  LED led_8 (.in(R1_reg_out[7]));
  Registre_8bits R1 (
    .value(R1_reg_out), .Write_perm(demultiplexer_1_out1[0]), .Read_perm(demultiplexer_1_out2[0]),
    .RAZ(demultiplexer_1_out3[0]), .clk(clock_1_out), .Reg_Out(R1_reg_out));
  Registre_8bits R2 (
    .value(R1_reg_out), .Write_perm(demultiplexer_1_out1[1]), .Read_perm(demultiplexer_1_out2[1]),
    .RAZ(demultiplexer_1_out3[1]), .clk(clock_1_out), .Reg_Out(R1_reg_out));
  Registre_8bits R3 (
    .value(R1_reg_out), .Write_perm(demultiplexer_1_out1[2]), .Read_perm(demultiplexer_1_out2[2]),
    .RAZ(demultiplexer_1_out3[2]), .clk(clock_1_out), .Reg_Out(R1_reg_out));
  Registre_8bits R7 (
    .value(R1_reg_out), .Write_perm(demultiplexer_1_out1[6]), .Read_perm(demultiplexer_1_out2[6]),
    .RAZ(demultiplexer_1_out3[6]), .clk(clock_1_out), .Reg_Out(R1_reg_out));
  Registre_8bits R4 (
    .value(R1_reg_out), .Write_perm(demultiplexer_1_out1[3]), .Read_perm(demultiplexer_1_out2[3]),
    .RAZ(demultiplexer_1_out3[3]), .clk(clock_1_out), .Reg_Out(R1_reg_out));
  Registre_8bits R5 (
    .value(R1_reg_out), .Write_perm(demultiplexer_1_out1[4]), .Read_perm(demultiplexer_1_out2[4]),
    .RAZ(demultiplexer_1_out3[4]), .clk(clock_1_out), .Reg_Out(R1_reg_out));
  Registre_8bits R6 (
    .value(R1_reg_out), .Write_perm(demultiplexer_1_out1[5]), .Read_perm(demultiplexer_1_out2[5]),
    .RAZ(demultiplexer_1_out3[5]), .clk(clock_1_out), .Reg_Out(R1_reg_out));
  Control_Unit control_unit_1 (
    .reset(in_1), .clk(clock_1_out), .NEG_FLAG(flag_reg_1_neg_flag), .ZERO_FLAG(flag_reg_1_zero_flag),
    .POS_FLAG(flag_reg_1_pos_flag), .Cu_Instruction(control_unit_1_cu_instruction),
    .value(control_unit_1_value), .vers_alu(control_unit_1_vers_alu));
  and and_1 (and_1_out, control_unit_1_cu_instruction[13], not_1_out);
  not not_1 (not_1_out, control_unit_1_cu_instruction[14]);
  not not_2 (not_2_out, control_unit_1_cu_instruction[13]);
  and and_2 (and_2_out, not_2_out, control_unit_1_cu_instruction[14]);
  and and_3 (and_3_out, control_unit_1_cu_instruction[13], control_unit_1_cu_instruction[14]);
  AB_Sub_Reg ab_sub_reg_1 (
    .Value_In(R1_reg_out), .A_perm(control_unit_1_cu_instruction[9]),
    .B_perm(control_unit_1_cu_instruction[10]), .clk(clock_1_out), .A_out(ab_sub_reg_1_a_out),
    .B_out(ab_sub_reg_1_b_out));  // open: RAZ
  ALU alu_1 (
    .A(ab_sub_reg_1_a_out), .B(ab_sub_reg_1_b_out), .OP_BIN(control_unit_1_cu_instruction[5:2]),
    .ALU_Perm(control_unit_1_cu_instruction[1]), .clk(clock_1_out), .JZ_port(control_unit_1_vers_alu),
    .ALU_Result(R1_reg_out), .NEG_FLAG(alu_1_neg_flag), .ZERO_FLAG(alu_1_zero_flag), .POS_FLAG(alu_1_pos_flag));  // open: Caryy_FLAG
  Flag_Reg flag_reg_1 (
    .NEG(alu_1_neg_flag), .ZERO(alu_1_zero_flag), .POS(alu_1_pos_flag), .clk(clock_1_out),
    .OP(control_unit_1_cu_instruction[5:2]), .NEG_FLAG(flag_reg_1_neg_flag),
    .ZERO_FLAG(flag_reg_1_zero_flag), .POS_FLAG(flag_reg_1_pos_flag));
  Bin_To_Dec bin_to_dec_1 (
    .bin1(control_unit_1_cu_instruction[6]), .bin2(control_unit_1_cu_instruction[7]),
    .bin3(control_unit_1_cu_instruction[8]), .N1(bin_to_dec_1_n1[0]), .N2(bin_to_dec_1_n1[1]),
    .N3(bin_to_dec_1_n1[2]), .N4(bin_to_dec_1_n1[3]), .N5(bin_to_dec_1_n1[4]), .N6(bin_to_dec_1_n1[5]),
    .N7(bin_to_dec_1_n1[6]));  // open: bin4, N8, N9, N10
  Registre_8bits work_reg (
    .value(R1_reg_out), .Write_perm(and_1_out), .Read_perm(and_2_out), .RAZ(and_3_out), .clk(clock_1_out),
    .Reg_Out(R1_reg_out));
  Pull_Resistor pull_resistor_1 (.node(R1_reg_out[0]));
  Pull_Resistor pull_resistor_2 (.node(R1_reg_out[1]));
  Pull_Resistor pull_resistor_3 (.node(R1_reg_out[2]));
  Pull_Resistor pull_resistor_4 (.node(R1_reg_out[3]));
  Pull_Resistor pull_resistor_5 (.node(R1_reg_out[4]));
  Pull_Resistor pull_resistor_6 (.node(R1_reg_out[5]));
  Pull_Resistor pull_resistor_7 (.node(R1_reg_out[6]));
  Pull_Resistor pull_resistor_8 (.node(R1_reg_out[7]));
  assign R1_reg_out = control_unit_1_cu_instruction[0] ? control_unit_1_value : 8'bz;  // Controlled_Buffer controlled_buffer_1
endmodule

module ALU (
  input  [7:0] A,
  input  [7:0] B,
  input  [3:0] OP_BIN,
  input  ALU_Perm,
  input  clk,
  input  JZ_port,
  output [7:0] ALU_Result,
  output NEG_FLAG,
  output ZERO_FLAG,
  output POS_FLAG,
  output Caryy_FLAG
);

  wire and_1_out, and_2_out, and_3_out, and_6_out, and_7_out, and_8_out, and_9_out, and_10_out, and_11_out,
       and_12_out, and_14_out, comparator_1_eq, comparator_1_lt, not_1_out, not_2_out, not_5_out, not_6_out,
       not_7_out, not_8_out, not_9_out, not_10_out, not_11_out, not_12_out, not_13_out, not_14_out,
       not_15_out, not_16_out, or_1_out, subtractor_1_bout;
  wire [7:0] adder_1_out, and_4_out, divider_1_out, multiplexer_1_out, multiplier_1_out, nand_1_out,
       nor_1_out, not_3_out, not_4_out, or_2_out, register_1_q, subtractor_1_out, xnor_1_out, xor_1_out;

  not not_1 (not_1_out, OP_BIN[1]);
  not not_2 (not_2_out, OP_BIN[0]);
  and and_1 (and_1_out, OP_BIN[0], not_1_out, OP_BIN[2], OP_BIN[3]);
  and and_2 (and_2_out, not_2_out, OP_BIN[1], OP_BIN[2], OP_BIN[3]);
  and and_3 (and_3_out, OP_BIN[0], OP_BIN[1], OP_BIN[2], OP_BIN[3]);
  or or_1 (or_1_out, and_1_out, and_2_out, and_3_out, JZ_port);
  Adder adder_1 (.a(A), .b(B), .out(adder_1_out), .cout(Caryy_FLAG));  // open: cin
  Subtractor subtractor_1 (.a(A), .b(B), .out(subtractor_1_out), .bout(subtractor_1_bout));  // open: bin
  Multiplier multiplier_1 (.a(A), .b(B), .out(multiplier_1_out));  // open: cin, cout
  Divider divider_1 (.a(A), .b(B), .out(divider_1_out));  // open: upper, rem
  assign and_4_out = A & B;  // AND_Gate and_4, 8 bits wide
  assign nand_1_out = ~(A & B);  // NAND_Gate nand_1, 8 bits wide
  assign or_2_out = A | B;  // OR_Gate or_2, 8 bits wide
  assign nor_1_out = ~(A | B);  // NOR_Gate nor_1, 8 bits wide
  assign xor_1_out = A ^ B;  // XOR_Gate xor_1, 8 bits wide
  assign xnor_1_out = ~(A ^ B);  // XNOR_Gate xnor_1, 8 bits wide
  assign not_3_out = ~A;  // NOT_Gate not_3, 8 bits wide
  assign not_4_out = ~B;  // NOT_Gate not_4, 8 bits wide
  Multiplexer #(.select(4), .width(8)) multiplexer_1 (
    .in0({8{1'b0}}), .in1(adder_1_out), .in2(subtractor_1_out), .in3(multiplier_1_out), .in4(divider_1_out),
    .in5(and_4_out), .in6(nand_1_out), .in7(or_2_out), .in8(nor_1_out), .in9(xor_1_out), .in10(xnor_1_out),
    .in11(not_3_out), .in12(not_4_out), .in13({8{1'b0}}), .in14({8{1'b0}}), .in15({8{1'b0}}),
    .out(multiplexer_1_out), .sel(OP_BIN));
  Comparator comparator_1 (.a(register_1_q), .b({8{1'b0}}), .eq(comparator_1_eq), .lt(comparator_1_lt));  // open: gt
  assign ALU_Result = ALU_Perm ? multiplexer_1_out : 8'bz;  // Controlled_Buffer controlled_buffer_1
  not not_5 (not_5_out, multiplexer_1_out[0]);
  not not_6 (not_6_out, multiplexer_1_out[1]);
  not not_7 (not_7_out, multiplexer_1_out[2]);
  not not_8 (not_8_out, multiplexer_1_out[3]);
  not not_9 (not_9_out, multiplexer_1_out[4]);
  not not_10 (not_10_out, multiplexer_1_out[5]);
  not not_11 (not_11_out, multiplexer_1_out[6]);
  not not_12 (not_12_out, multiplexer_1_out[7]);
  Register register_1 (.D(multiplexer_1_out), .en(not_13_out), .clk(clk), .Q(register_1_q));  // open: clr
  not not_13 (not_13_out, or_1_out);
  or or_3 (ZERO_FLAG, comparator_1_eq, and_14_out);
  and and_5 (NEG_FLAG, subtractor_1_bout, comparator_1_lt);
  and and_6 (and_6_out, not_6_out, not_5_out);
  and and_7 (and_7_out, and_6_out, not_7_out);
  and and_8 (and_8_out, and_7_out, not_8_out);
  and and_9 (and_9_out, and_8_out, not_9_out);
  and and_10 (and_10_out, and_9_out, not_10_out);
  and and_11 (and_11_out, and_10_out, not_11_out);
  and and_12 (and_12_out, and_11_out, not_12_out);
  and and_13 (POS_FLAG, not_14_out, not_15_out);
  not not_14 (not_14_out, NEG_FLAG);
  not not_15 (not_15_out, ZERO_FLAG);
  and and_14 (and_14_out, and_12_out, not_16_out);
  not not_16 (not_16_out, or_1_out);
endmodule

module Registre_8bits (
  input  [7:0] value,
  input  Write_perm,
  input  Read_perm,
  input  RAZ,
  input  clk,
  output [7:0] Reg_Out
);

  wire [7:0] register_1_q;

  Register register_1 (.D(value), .en(Write_perm), .clk(clk), .Q(register_1_q), .clr(RAZ));
  assign Reg_Out = Read_perm ? register_1_q : 8'bz;  // Controlled_Buffer controlled_buffer_1
endmodule

module Bin_To_Dec (
  input  bin1,
  input  bin2,
  input  bin3,
  input  bin4,
  output N1,
  output N2,
  output N3,
  output N4,
  output N5,
  output N6,
  output N7,
  output N8,
  output N9,
  output N10
);

  wire not_1_out, not_2_out, not_3_out, not_4_out;

  not not_1 (not_1_out, bin1);
  not not_2 (not_2_out, bin2);
  not not_3 (not_3_out, bin3);
  not not_4 (not_4_out, bin4);
  and and_1 (N1, bin1, not_2_out, not_3_out, not_4_out);
  and and_2 (N2, not_1_out, bin2, not_3_out, not_4_out);
  and and_3 (N3, bin1, bin2, not_3_out, not_4_out);
  and and_4 (N4, bin3, not_4_out, not_1_out, not_2_out);
  and and_5 (N5, bin1, not_2_out, bin3, not_4_out);
  and and_6 (N6, not_1_out, bin2, bin3, not_4_out);
  and and_7 (N7, bin1, bin2, bin3, not_4_out);
  and and_8 (N8, not_1_out, not_2_out, not_3_out, bin4);
  and and_9 (N9, bin1, not_2_out, not_3_out, bin4);
  and and_10 (N10, not_1_out, bin2, not_3_out, bin4);
endmodule

module AB_Sub_Reg (
  input  [7:0] Value_In,
  input  A_perm,
  input  B_perm,
  input  clk,
  input  RAZ,
  output [7:0] A_out,
  output [7:0] B_out
);

  Register register_1 (.D(Value_In), .en(A_perm), .clk(clk), .Q(A_out), .clr(RAZ));
  Register register_2 (.D(Value_In), .en(B_perm), .clk(clk), .Q(B_out), .clr(RAZ));
endmodule

module Control_Unit_Part01 (
  input  [7:0] value_bin,
  input  r1,
  input  r2,
  input  r3,
  input  r4,
  input  r5,
  input  r6,
  input  r7,
  input  add,
  input  sub,
  input  mult,
  input  div,
  input  op_and,
  input  op_nand,
  input  op_or,
  input  op_nor,
  input  op_xor,
  input  op_xnor,
  input  not_A,
  input  not_B,
  input  write,
  input  read,
  input  clear,
  input  halt,
  input  jump_if_0,
  input  jump_if_neg,
  input  jump_if_pos,
  output [7:0] value_out,
  output [2:0] reg_bin,
  output [4:0] CU_Op_Bin
);

  or or_1 (reg_bin[0], r1, r3, r5, r7);
  or or_2 (reg_bin[1], r2, r3, r6, r7);
  or or_3 (reg_bin[2], r4, r5, r6, r7);
  or or_4 (CU_Op_Bin[0], jump_if_0, add, mult, op_and, op_or, op_xor, not_A, write, clear, jump_if_pos);
  or or_5 (CU_Op_Bin[1], sub, mult, op_nand, op_or, op_xnor, not_A, read, clear, jump_if_neg, jump_if_pos);
  or or_6 (CU_Op_Bin[2], div, op_and, op_nand, op_or, not_B, write, read, clear);
  or or_7 (CU_Op_Bin[3], op_nor, op_xor, op_xnor, not_A, not_B, write, read, clear);
  or or_8 (CU_Op_Bin[4], halt, jump_if_0, jump_if_neg, jump_if_pos);

  assign value_out = value_bin;
endmodule

module Control_Unit (
  input  reset,
  input  clk,
  input  NEG_FLAG,
  input  ZERO_FLAG,
  input  POS_FLAG,
  output [14:0] Cu_Instruction,
  output [7:0] value,
  output vers_alu
);

  wire and_1_out, and_2_out, and_3_out, and_4_out, and_5_out, and_6_out, and_7_out, and_8_out, and_9_out,
       and_10_out, d_ff_1_q, d_ff_1_qn, not_1_out, not_2_out, not_3_out, not_4_out, not_5_out, not_6_out,
       not_7_out, not_8_out, not_9_out, or_1_out, or_2_out;
  wire [7:0] counter_1_q, multiplier_1_out, subtractor_1_out;

  or or_1 (or_1_out, and_3_out, and_5_out, and_7_out, and_9_out);
  D_Flip_Flop #(.trigger("high")) d_ff_1 (
    .D(and_2_out), .clk(and_2_out), .Q(d_ff_1_q), .Qn(d_ff_1_qn), .reset(reset));  // open: preset
  or or_2 (or_2_out, d_ff_1_q, reset);
  and and_1 (and_1_out, clk, d_ff_1_qn);
  Counter counter_1 (
    .clr(or_2_out), .load(or_1_out), .up(1'b1), .clk(and_1_out), .D(multiplier_1_out), .Q(counter_1_q));  // open: count, carry
  Multiplier multiplier_1 (.a(8'h8), .b(subtractor_1_out), .out(multiplier_1_out));  // open: cin, cout
  Subtractor subtractor_1 (.a(value), .b(8'h1), .out(subtractor_1_out));  // open: bin, bout
  and and_2 (and_2_out, counter_1_q[7], counter_1_q[6], counter_1_q[5], counter_1_q[4], counter_1_q[3], counter_1_q[2], counter_1_q[1], counter_1_q[0]);
  not not_1 (not_1_out, Cu_Instruction[3]);
  not not_2 (not_2_out, Cu_Instruction[2]);
  and and_3 (and_3_out, Cu_Instruction[2], not_1_out, Cu_Instruction[4], Cu_Instruction[5]);
  and and_4 (and_4_out, not_2_out, Cu_Instruction[3], Cu_Instruction[4], Cu_Instruction[5]);
  and and_5 (and_5_out, and_4_out, POS_FLAG);
  and and_6 (and_6_out, Cu_Instruction[2], Cu_Instruction[3], Cu_Instruction[4], Cu_Instruction[5]);
  and and_7 (and_7_out, and_6_out, NEG_FLAG);
  not not_3 (not_3_out, Cu_Instruction[6]);
  not not_4 (not_4_out, Cu_Instruction[7]);
  not not_5 (not_5_out, Cu_Instruction[8]);
  and and_8 (and_8_out, not_3_out, not_4_out, not_5_out, Cu_Instruction[11], Cu_Instruction[12]);
  ROM #(.dataWidth(15)) Instructions_ROM (.addr(counter_1_q), .data(Cu_Instruction));
  and and_9 (and_9_out, ZERO_FLAG, and_8_out);
  not not_6 (not_6_out, Cu_Instruction[2]);
  not not_7 (not_7_out, Cu_Instruction[3]);
  not not_8 (not_8_out, Cu_Instruction[4]);
  not not_9 (not_9_out, Cu_Instruction[5]);
  ROM Data_ROM (.addr(counter_1_q), .data(value));
  and and_10 (and_10_out, not_6_out, not_7_out, not_8_out, not_9_out);
  or or_3 (vers_alu, and_8_out, and_10_out);

  // Notes on the sheet:
  //   contents of Instructions_ROM (hex, n*v repeats v):
  //   10c0 7*0 841 41 40 5*0 881 81 80 5*0 34 7*0 10c0 30c0 10c0 4840 4040 40 0 0 34 7*0 1248 1048 1488
  //   1088 8ca ca 8 8 1288 1088 14c8 10c8 90a 10a 8 8 38 7*0 3c 7*0 1800 7*0 1080 3080 1080 4840 4040 40 0
  //   0 10c0 30c0 10c0 4880 4080 80 0 0 34 7*0 10c0 30c0 10c0 4840 4040 40 0 0 34 7*0 1288 1088 1448 1048
  //   8ca ca 8 8 1248 1048 14c8 10c8 90a 10a 8 8 38 7*0 3c 7*0 1800 7*0 1040 3040 1040 4880 4080 80 0 0
  //   10c0 30c0 10c0 4840 4040 40 0 0 34 7*0 10c0 30c0 10c0 4880 4080 80 0 0 34 7*0 1248 1048 1488 1088
  //   8ca ca 8 8 1800 7*0 38 7*0 3c
  //   contents of Data_ROM (hex, n*v repeats v):
  //   8*0 fc fc fc 5*0 c6 c6 c6 5*0 1b 15*0 1f 23*0 c 7*0 f 7*0 1f 23*0 7 15*0 7 23*0 16 7*0 19 7*0 1f
  //   23*0 11 15*0 11 15*0 1f 7*0 7 7*0 11
endmodule

module decoder_to_dec_2bin (
  input  in_1,
  input  in_2,
  output N0,
  output N1,
  output N2,
  output N3
);

  wire not_1_out, not_2_out;

  not not_1 (not_1_out, in_1);
  not not_2 (not_2_out, in_2);
  and and_1 (N0, not_1_out, not_2_out);
  and and_2 (N1, in_1, not_2_out);
  and and_3 (N2, in_2, not_1_out);
  and and_4 (N3, in_2, in_1);
endmodule

module Flag_Reg (
  input  NEG,
  input  ZERO,
  input  POS,
  input  clk,
  input  [3:0] OP,
  output NEG_FLAG,
  output ZERO_FLAG,
  output POS_FLAG
);

  wire and_1_out, and_2_out, and_3_out, not_1_out, not_2_out, not_3_out, or_1_out;

  not not_1 (not_1_out, OP[1]);
  and and_1 (and_1_out, OP[0], not_1_out, OP[2], OP[3]);
  not not_2 (not_2_out, OP[0]);
  and and_2 (and_2_out, not_2_out, OP[1], OP[2], OP[3]);
  and and_3 (and_3_out, OP[0], OP[1], OP[2], OP[3]);
  or or_1 (or_1_out, and_1_out, and_2_out, and_3_out);
  Register #(.width(1)) register_1 (.D(NEG), .en(not_3_out), .clk(clk), .Q(NEG_FLAG));  // open: clr
  Register #(.width(1)) register_2 (.D(ZERO), .en(not_3_out), .clk(clk), .Q(ZERO_FLAG));  // open: clr
  Register #(.width(1)) register_3 (.D(POS), .en(not_3_out), .clk(clk), .Q(POS_FLAG));  // open: clr
  not not_3 (not_3_out, or_1_out);
endmodule
